# Fritzing sketch schematic (saved by Fritzing 0.9.1b)
breadboards: 1

parts:
  part = Arduino Uno (Rev3)
  U1 = POT [package=alps_pot]
  LED5 = smd LED [color="Red (633nm)" package="0603 [SMD]"]
  R2 = Resistor [tolerance=±5% resistance=330 package="0805 [SMD]"]
  LED6 = smd LED [color="Red (633nm)" package="0603 [SMD]"]
  R3 = Resistor [tolerance=±5% resistance=330 package="0805 [SMD]"]
  LED7 = smd LED [color="Red (633nm)" package="0603 [SMD]"]
  R4 = Resistor [tolerance=±5% resistance=330 package="0805 [SMD]"]
  LED8 = smd LED [color="Red (633nm)" package="0603 [SMD]"]
  R5 = Resistor [tolerance=±5% resistance=330 package="0805 [SMD]"]
  LED1 = smd LED [color="Red (633nm)" package="0603 [SMD]"]
  LED4 = smd LED [color="Red (633nm)" package="0603 [SMD]"]
  LED3 = smd LED [color="Red (633nm)" package="0603 [SMD]"]
  LED2 = smd LED [color="Red (633nm)" package="0603 [SMD]"]
  R6 = Resistor [tolerance=±5% resistance=330 package="0805 [SMD]"]
  R7 = Resistor [tolerance=±5% resistance=330 package="0805 [SMD]"]
  R8 = Resistor [tolerance=±5% resistance=330 package="0805 [SMD]"]
  R9 = Resistor [tolerance=±5% resistance=330 package="0805 [SMD]"]
  J1 = Piezo Speaker

nets:
  N1: part.A0, U1.S
  N2: part.D8, LED8.anode
  N3: part.D11_PWM/MOSI, J1.pin1
  N4: part.D12/MISO, LED1.anode
  N5: part.GND, U1.A, R2.Pin_1, R3.Pin_1, R4.Pin_1, R5.Pin_1, R6.Pin_1, R7.Pin_1, R8.Pin_1, R9.Pin_1, J1.pin2
  N6: part.D2, LED2.anode
  N7: part.D3_PWM, LED3.anode
  N8: part.D4, LED4.anode
  N9: part.D5_PWM, LED5.anode
  N10: part.D6_PWM, LED6.anode
  N11: part.D7, LED7.anode
  N12: part.5V, U1.E
